# Fritzing sketch Car LED Controller (saved by Fritzing 0.9.10b)
breadboards: 2

parts:
  U1 = LuaNode32 / ESP32 [part_number=ESP32S-PIN30]
  U2 = LCD-16X2 [package=lcd-16x2_noholes]
  U5 = WS2812 RGB LED strip
  U3 = POT [knob_status=50% power=0.5W package=alps_pot]
  R2 = Resistor [tolerance=±5% resistance=1M package="1206 [SMD]"]
  R3 = Resistor [tolerance=±5% resistance=47k package="1206 [SMD]"]
  C1 = Capacitor [package=cap-pth-small2]
  R4 = Resistor [tolerance=±5% resistance=1M package="1206 [SMD]"]
  R5 = Resistor [tolerance=±5% resistance=1M package="1206 [SMD]"]
  R6 = Resistor [tolerance=±5% resistance=1M package="1206 [SMD]"]
  R7 = Resistor [tolerance=±5% resistance=47k package="1206 [SMD]"]
  R8 = Resistor [tolerance=±5% resistance=47k package="1206 [SMD]"]
  R9 = Resistor [tolerance=±5% resistance=47k package="1206 [SMD]"]
  C2 = Capacitor [package=cap-pth-small2]
  C3 = Capacitor [package=cap-pth-small2]
  C4 = Capacitor [package=cap-pth-small2]
  S2 = Momentary Switch [package=ksa_sealed_tac_switch]
  S1 = Momentary Switch [package=ksa_sealed_tac_switch]
  R10 = Resistor [tolerance=±5% resistance=1M package="1206 [SMD]"]
  M1 = RioRand LM2596
  M2 = RioRand LM2596
  JP1 = Header 4 [package=molex-1x4_lock]
  JP2 = Header 4 [package=molex-1x4_lock]

nets:
  N1: U1.VP, R6.Pin_1, C2.2
  N2: U1.VN, R5.Pin_0, C3.2
  N3: U1.D34, R4.Pin_0, C4.2
  N4: U1.D35, R2.Pin_0, C1.2
  N5: U1.D32, U2.RS
  N6: U1.D33, U2.E
  N7: U1.D25, U2.DB4
  N8: U1.D26, U2.DB5
  N9: U1.D27, U2.DB6
  N10: U1.D14, U2.DB7
  GND: U1.GND, U2.VSS, U2.R_W, U3.E, R3.Pin_1, C1.1, R7.Pin_1, R8.Pin_1, R9.Pin_1, C2.1, C3.1, C4.1, R10.Pin_0, M2.Pin_4
  VIN: U1.Vin, U2.VDD, U2.A, U3.A, M2.Pin_3
  N11: U1.TX0, S2.3, S2.4
  N12: U1.D22, S2.1, S2.2, R10.Pin_1
  N13: U1.D23, U5.DIN
  N14: U2.VO, U3.S
  N15: U5.GND, M1.Pin_4
  N16: U5.VCC, M1.Pin_3
  N17: R2.Pin_1, JP1.4
  N18: R4.Pin_1, JP1.3
  N19: R5.Pin_1, S1.1, S1.2
  N20: R6.Pin_0, JP1.1
  N21: S1.3, S1.4, JP1.2
  N22: M1.Pin_1, M2.Pin_1, JP2.1
  N23: M1.Pin_2, M2.Pin_2, JP2.4

custom parts:
  LuaNode32 / ESP32: New Image for LuaNode32 DOIT ESP32 DEVKIT V1. Base parts from LuaNode32 / ESP32 ESP32 based LuaNode32 by G.Noorlander DOIT Esp32 DevKit v1 (30 pins long, 11 pins width) by Werner Rothschopf (modified by vanepp Dec 2018)
  WS2812 RGB LED strip: WS2812 strip
